# Fritzing sketch RPI RGB LED WS2812B (saved by Fritzing 0.9.3b)

parts:
  Raspberry_Pi_1 = Raspberry Pi 3 [part_number=RPI-3-V1.2]
  RGB_SMD_LED2 = SMD RGB LED (WS2812) [package=5050]  # not connected
  RGB_SMD_LED3 = SMD RGB LED (WS2812) [package=5050]  # not connected
  RGB_SMD_LED4 = SMD RGB LED (WS2812) [package=5050]  # not connected
  RGB_SMD_LED5 = SMD RGB LED (WS2812) [package=5050]  # not connected
  RGB_SMD_LED6 = SMD RGB LED (WS2812) [package=5050]  # not connected
  RGB_SMD_LED7 = SMD RGB LED (WS2812) [package=5050]  # not connected
  RGB_SMD_LED8 = SMD RGB LED (WS2812) [package=5050]  # not connected
  RGB_SMD_LED9 = SMD RGB LED (WS2812) [package=5050]  # not connected
  RGB_SMD_LED1 = SMD RGB LED (WS2812) [package=5050]

nets:
  N1: Raspberry_Pi_1.GIPO18, RGB_SMD_LED1.DIn
  N2: Raspberry_Pi_1.GND, RGB_SMD_LED1.DOut
  5V: Raspberry_Pi_1.5V, RGB_SMD_LED1.VCC
