# Fritzing sketch RPI 8 CHANNEL RELAY PASSIVE IR INDICATOR(PIR) (saved by Fritzing 0.9.3b)

parts:
  Raspberry_Pi_1 = Raspberry Pi 3 [part_number=RPI-3-V1.2]
  8_Channel_Relay1 = 8 Channel Power Relay
  PIR1 = PIR sensor

nets:
  3V3: Raspberry_Pi_1.3v3, PIR1.VDD
  N1: Raspberry_Pi_1.GIPO4, PIR1.SIG
  GND: Raspberry_Pi_1.GND, Raspberry_Pi_1.GIPO5, Raspberry_Pi_1.GIPO13, 8_Channel_Relay1.GND, 8_Channel_Relay1.IN1, 8_Channel_Relay1.IN3, PIR1.GND
  N2: Raspberry_Pi_1.GIPO6, Raspberry_Pi_1.GIPO12, 8_Channel_Relay1.IN2
  N3: Raspberry_Pi_1.GIPO19, 8_Channel_Relay1.IN4
  N4: Raspberry_Pi_1.GIPO26, 8_Channel_Relay1.IN5
  N5: Raspberry_Pi_1.GIPO21, 8_Channel_Relay1.IN8
  N6: Raspberry_Pi_1.GIPO20, 8_Channel_Relay1.IN7
  N7: Raspberry_Pi_1.GIPO16, 8_Channel_Relay1.IN6
  5V: Raspberry_Pi_1.5V, 8_Channel_Relay1.VCC

custom parts:
  8 Channel Power Relay: An 8 channel power relay. The module operates at 5V.
